# Fritzing sketch controller (saved by Fritzing 0.7.7b)

parts:
  Arduino_Nano = Arduino Nano v2.3
  Rpd = Resistor [tolerance=±5% resistance=1k package=THT]
  MTR_SW = female pin header, 2 pins [form="♀ (female)"]
  SMDv2_3 = female pin header, 4 pins [form="♀ (female)"]
  -5V+ = female pin header, 2 pins [form="♀ (female)"]
  POTI = Rotary Potentiometer (Small) [maximum_resistance=100kΩ]

nets:
  N1: Arduino_Nano.GND, MTR_SW.pin2, SMDv2_3.pin1, -5V+.pin2, POTI.leg1
  N2: Arduino_Nano.D2, Rpd.Pin_0
  N3: Arduino_Nano.D4, SMDv2_3.pin2
  N4: Arduino_Nano.D5, SMDv2_3.pin3
  N5: Arduino_Nano.D6, SMDv2_3.pin4
  N6: Arduino_Nano.AREF, POTI.leg2
  N7: Arduino_Nano.A2, POTI.wiper
  N8: Arduino_Nano.VIN, -5V+.pin1
  N9: Rpd.Pin_1, MTR_SW.pin1
